# Fritzing sketch Z8 Schematic 1 Lab 1 (saved by Fritzing 0.9.4)
breadboards: 1

parts:
  Part1 = Arduino Uno (Rev3)
  R1 = Resistor [tolerance=±5% resistance=220 package=THT]
  J1 = Basic Force Sensing Resistor (FSR) [package=THT]
  LED1 = smd LED [color="Red (633nm)" package="0603 [SMD]"]

nets:
  N1: Part1.A2, R1.Pin_1, J1.pin_0
  N2: Part1.D13/SCK, LED1.anode
  N3: Part1.GND, R1.Pin_0, LED1.cathode
  N4: Part1.5V, J1.pin_1
