# Fritzing sketch Z8 Schematic 2 Lab 1 (saved by Fritzing 0.9.4)
breadboards: 1

parts:
  Part1 = Arduino Uno (Rev3)
  LED1 = smd LED [color="Green (555nm)" package="0805 [SMD]"]
  LED2 = smd LED [color="Green (555nm)" package="0805 [SMD]"]
  R1 = Resistor [tolerance=±5% resistance=220 package="0603 [SMD]"]
  R2 = Resistor [tolerance=±5% resistance=220 package="0603 [SMD]"]
  LED3 = smd LED [color="Yellow (595nm)" package="0805 [SMD]"]
  LED4 = smd LED [color="Yellow (595nm)" package="0805 [SMD]"]
  R3 = Resistor [tolerance=±5% resistance=220 package="0603 [SMD]"]
  R4 = Resistor [tolerance=±5% resistance=220 package="0603 [SMD]"]
  LED5 = smd LED [color="Red (633nm)" package="0805 [SMD]"]
  LED6 = smd LED [color="Red (633nm)" package="0805 [SMD]"]
  R6 = Resistor [tolerance=±5% resistance=220 package="0603 [SMD]"]
  T1 = LM35 Temperature Sensor [package="TO92 [THT]"]
  R5 = Resistor [tolerance=±5% resistance=220 package="0603 [SMD]"]

nets (from the schematic view):
  N1: Part1.D2, LED2.cathode
  N2: Part1.D3_PWM, LED1.cathode, R2.Pin_1
  N3: Part1.D4, LED3.cathode
  N4: Part1.D5_PWM, R3.Pin_1
  N5: Part1.D6_PWM, LED6.cathode, R5.Pin_1
  N6: Part1.D7, LED5.cathode
  N7: Part1.5V, T1.+Vs
  N8: LED1.anode, R2.Pin_0
  N9: LED2.anode, R5.Pin_0
  N10: R1.Pin_0, LED4.anode, R4.Pin_0, R6.Pin_0
  N11: R1.Pin_1, LED6.anode
  N12: LED3.anode, R3.Pin_0
  N13: LED4.cathode, R4.Pin_1
  N14: LED5.anode, R6.Pin_1
